// Logisim project Circuito.circ as structural Verilog: 7 circuits, main circuit main
module main (
  input  [2:0] Jugador_Fijo,
  input  [2:0] Jugador_2,
  output [3:0] Victorias
);

  wire button_1_out, clock_1_out;

  Clock clock_1 (.out(clock_1_out));
  Button button_1 (.out(button_1_out));
  CircuitoPrincipal circuitoprincipal_1 (
    .in_1(clock_1_out), .in_3(Jugador_Fijo), .in_4(Jugador_2), .in_2(button_1_out), .out_5(Victorias));

  // Notes on the sheet:
  //   CLK
  //   Botón
endmodule

module winner (
  input  [2:0] in_1,
  input  [2:0] in_2,
  output [2:0] out_3
);

  wire and_1_out, and_2_out, and_3_out, and_4_out, and_5_out, and_6_out, and_7_out, and_8_out, and_9_out,
       and_10_out, and_11_out, and_12_out, and_13_out, and_14_out, and_15_out, and_16_out, not_1_out,
       not_2_out, not_3_out, not_4_out, not_5_out, not_6_out, not_7_out, not_8_out, not_9_out, not_10_out,
       not_11_out, not_12_out;

  not not_1 (not_1_out, in_1[1]);
  not not_2 (not_2_out, in_1[0]);
  not not_3 (not_3_out, in_2[1]);
  not not_4 (not_4_out, in_2[0]);
  not not_5 (not_5_out, in_1[0]);
  not not_6 (not_6_out, in_2[0]);
  not not_7 (not_7_out, in_1[0]);
  not not_8 (not_8_out, in_2[0]);
  not not_9 (not_9_out, in_1[1]);
  not not_10 (not_10_out, in_1[2]);
  not not_11 (not_11_out, in_2[1]);
  not not_12 (not_12_out, in_2[2]);
  and and_1 (and_1_out, not_1_out, not_2_out, in_2[2], in_2[0]);
  and and_2 (and_2_out, in_2[2], in_2[1]);
  and and_3 (and_3_out, in_1[1], in_1[0], in_2[2], in_2[0]);
  and and_4 (and_4_out, in_1[2], in_1[0], not_3_out, not_4_out);
  and and_5 (and_5_out, in_1[2], in_1[0], in_2[1], in_2[0]);
  and and_6 (and_6_out, in_1[2], in_1[1]);
  and and_7 (and_7_out, not_5_out, in_2[1]);
  and and_8 (and_8_out, in_2[1], not_6_out);
  and and_9 (and_9_out, in_2[2], in_2[1]);
  and and_10 (and_10_out, in_1[1], not_7_out);
  and and_11 (and_11_out, in_1[1], not_8_out);
  and and_12 (and_12_out, in_1[2], in_1[1]);
  and and_13 (and_13_out, not_9_out, in_2[0]);
  and and_14 (and_14_out, not_10_out, in_2[2], in_2[1], in_2[0]);
  and and_15 (and_15_out, in_1[0], not_11_out);
  and and_16 (and_16_out, in_1[2], in_1[1], in_1[0], not_12_out);
  or or_1 (out_3[2], and_1_out, and_2_out, and_3_out, and_4_out, and_5_out, and_6_out);
  or or_2 (out_3[1], and_7_out, and_8_out, and_9_out, and_10_out, and_11_out, and_12_out);
  or or_3 (out_3[0], and_13_out, and_14_out, and_15_out, and_16_out);
endmodule

module D_FF (
  input  in_1,
  input  in_2,
  output out_3,
  output out_4
);

  wire and_1_out, and_2_out, and_3_out, and_4_out, nor_1_out, nor_2_out, not_1_out, not_2_out, not_3_out;

  not not_1 (not_1_out, in_1);
  not not_2 (not_2_out, in_2);
  and and_1 (and_1_out, not_1_out, not_2_out);
  and and_2 (and_2_out, in_2, not_1_out);
  not not_3 (not_3_out, nor_1_out);
  nor nor_1 (nor_1_out, and_1_out, nor_2_out);
  nor nor_2 (nor_2_out, nor_1_out, and_2_out);
  and and_3 (and_3_out, in_1, not_3_out);
  and and_4 (and_4_out, in_1, nor_1_out);
  nor nor_3 (out_3, and_3_out, out_4);
  nor nor_4 (out_4, out_3, and_4_out);

  // Notes on the sheet:
  //   ClK
  //   D
endmodule

module counter (
  input  X,
  input  Reset,
  input  CLK,
  output [3:0] out_4
);

  wire and_1_out, and_2_out, and_3_out, and_4_out, and_5_out, and_6_out, and_7_out, and_8_out, and_9_out,
       and_10_out, and_11_out, and_12_out, and_13_out, and_14_out, and_15_out, and_16_out, and_17_out,
       d_ff_1_out_3, d_ff_1_out_4, d_ff_2_out_3, d_ff_2_out_4, d_ff_3_out_3, d_ff_3_out_4, d_ff_4_out_3,
       d_ff_4_out_4, not_1_out, or_1_out, or_2_out, or_3_out, or_4_out;

  and and_1 (and_1_out, not_1_out, d_ff_3_out_3);
  and and_2 (and_2_out, d_ff_3_out_3, d_ff_2_out_4);
  and and_3 (and_3_out, not_1_out, d_ff_1_out_3);
  and and_4 (and_4_out, d_ff_4_out_3, d_ff_2_out_3, X, d_ff_3_out_3);
  and and_5 (and_5_out, not_1_out, d_ff_2_out_3);
  and and_6 (and_6_out, d_ff_2_out_3, d_ff_1_out_4);
  and and_7 (and_7_out, X, d_ff_1_out_4);
  and and_8 (and_8_out, d_ff_1_out_3, X, d_ff_2_out_4);
  and and_9 (and_9_out, d_ff_4_out_3, d_ff_3_out_3, d_ff_2_out_3);
  and and_10 (and_10_out, X, d_ff_2_out_3, d_ff_1_out_3, d_ff_3_out_4);
  and and_11 (and_11_out, d_ff_2_out_3, d_ff_1_out_4, d_ff_3_out_3);
  and and_12 (and_12_out, X, d_ff_1_out_3, d_ff_2_out_3, d_ff_3_out_3);
  and and_13 (and_13_out, d_ff_4_out_3, d_ff_3_out_3);
  or or_1 (or_1_out, and_3_out, and_7_out, and_4_out);
  or or_2 (or_2_out, and_9_out, and_5_out, and_8_out, and_6_out);
  or or_3 (or_3_out, and_1_out, and_10_out, and_13_out, and_11_out, and_2_out);
  or or_4 (or_4_out, d_ff_4_out_3, and_12_out);
  D_FF d_ff_1 (.in_1(CLK), .in_2(and_17_out), .out_3(d_ff_1_out_3), .out_4(d_ff_1_out_4));
  D_FF d_ff_2 (.in_1(CLK), .in_2(and_14_out), .out_3(d_ff_2_out_3), .out_4(d_ff_2_out_4));
  D_FF d_ff_3 (.in_1(CLK), .in_2(and_15_out), .out_3(d_ff_3_out_3), .out_4(d_ff_3_out_4));
  D_FF d_ff_4 (.in_1(CLK), .in_2(and_16_out), .out_3(d_ff_4_out_3), .out_4(d_ff_4_out_4));
  not not_1 (not_1_out, X);
  and and_14 (and_14_out, Reset, or_2_out);
  and and_15 (and_15_out, Reset, or_3_out);
  and and_16 (and_16_out, Reset, or_4_out);
  and and_17 (and_17_out, or_1_out, Reset);
  D_FF d_ff_5 (.in_1(CLK), .in_2(and_17_out), .out_3(out_4[0]));  // open: out_4
  D_FF d_ff_6 (.in_1(CLK), .in_2(and_14_out), .out_3(out_4[1]));  // open: out_4
  D_FF d_ff_7 (.in_1(CLK), .in_2(and_15_out), .out_3(out_4[2]));  // open: out_4
  D_FF d_ff_8 (.in_1(CLK), .in_2(and_16_out), .out_3(out_4[3]));  // open: out_4

  // Notes on the sheet:
  //   ABCD~A~B~C~DX~X
  //   FFA
  //   FFB
  //   FFC
  //   FFD
  //   S
endmodule

module comparator (
  input  [2:0] in_1,
  input  [2:0] in_2,
  output out_3
);

  wire xnor_1_out, xnor_2_out, xnor_3_out;

  xnor xnor_1 (xnor_1_out, in_1[0], in_2[0]);
  xnor xnor_2 (xnor_2_out, in_2[1], in_1[1]);
  xnor xnor_3 (xnor_3_out, in_1[2], in_2[2]);
  and and_1 (out_3, xnor_1_out, xnor_2_out, xnor_3_out);
endmodule

module lastPlayer (
  input  [2:0] in_1,
  input  in_2,
  output [2:0] out_3
);

  D_FF d_ff_1 (.in_1(in_2), .in_2(in_1[2]), .out_3(out_3[2]));  // open: out_4
  D_FF d_ff_2 (.in_1(in_2), .in_2(in_1[1]), .out_3(out_3[1]));  // open: out_4
  D_FF d_ff_3 (.in_1(in_2), .in_2(in_1[0]), .out_3(out_3[0]));  // open: out_4
endmodule

module CircuitoPrincipal (
  input  in_1,
  input  in_2,
  input  [2:0] in_3,
  input  [2:0] in_4,
  output [3:0] out_5
);

  wire and_1_out, and_2_out, comparator_1_out_3, comparator_2_out_3, not_1_out, not_2_out, not_3_out;
  wire [2:0] lastplayer_1_out_3, winner_1_out_3;

  not not_1 (not_1_out, in_1);
  winner winner_1 (.in_1(in_3), .in_2(in_4), .out_3(winner_1_out_3));
  lastPlayer lastplayer_1 (.out_3(lastplayer_1_out_3), .in_1(in_3), .in_2(not_1_out));
  comparator comparator_1 (.in_1(lastplayer_1_out_3), .in_2(in_3), .out_3(comparator_1_out_3));
  comparator comparator_2 (.in_1(in_3), .in_2(winner_1_out_3), .out_3(comparator_2_out_3));
  and and_1 (and_1_out, in_1, not_2_out);
  and and_2 (and_2_out, comparator_1_out_3, not_3_out);
  not not_2 (not_2_out, in_2);
  counter counter_1 (.Reset(and_2_out), .CLK(and_1_out), .out_4(out_5), .X(comparator_2_out_3));
  not not_3 (not_3_out, in_2);
endmodule
